// Logisim project Tower of Hanoi -  Logisim.circ as structural Verilog: 4 circuits, main circuit main
module main (
  input  in_1,
  output Top,
  output out_3,
  output out_4,
  output Bottom
);

  wire and_1_out, and_2_out, and_3_out, and_4_out, and_5_out, and_6_out, not_1_out, or_1_out, t_ff_1_q,
       t_ff_1_qn, t_ff_2_q, t_ff_2_qn, t_ff_3_q, t_ff_3_qn, t_ff_4_q;

  T_Flip_Flop t_ff_1 (.clk(in_1), .T(1'b1), .Q(t_ff_1_q), .Qn(t_ff_1_qn), .en(or_1_out));  // open: preset, reset
  and _1 (Top, 1'b1, t_ff_1_q);
  and and_1 (and_1_out, 1'b1, t_ff_1_q);
  and and_2 (and_2_out, t_ff_1_qn, 1'b1);
  T_Flip_Flop t_ff_2 (.clk(in_1), .T(and_1_out), .Q(t_ff_2_q), .Qn(t_ff_2_qn), .en(or_1_out));  // open: preset, reset
  and _2 (out_3, and_2_out, t_ff_2_q);
  and and_3 (and_3_out, and_1_out, t_ff_2_q);
  and and_4 (and_4_out, t_ff_2_qn, and_2_out);
  T_Flip_Flop t_ff_3 (.clk(in_1), .T(and_3_out), .Q(t_ff_3_q), .Qn(t_ff_3_qn), .en(or_1_out));  // open: preset, reset
  and _3 (out_4, and_4_out, t_ff_3_q);
  and and_5 (and_5_out, and_3_out, t_ff_3_q);
  and and_6 (and_6_out, t_ff_3_qn, and_4_out);
  and _4 (Bottom, and_6_out, t_ff_4_q);
  or or_1 (or_1_out, t_ff_1_q, t_ff_2_q, t_ff_3_q, not_1_out);
  not not_1 (not_1_out, t_ff_4_q);
  T_Flip_Flop t_ff_4 (.clk(in_1), .T(and_5_out), .Q(t_ff_4_q), .en(or_1_out));  // open: Qn, preset, reset
endmodule

module Display (
  input  row_d,
  input  Clock,
  output [3:0] out_3,
  output ToPeg_Byte_1,
  output ToPeg_Byte_0,
  output FromPeg_Byte_1,
  output FromPeg_Byte_0
);

  wire nand_1_out, nand_2_out;

  D_Flip_Flop d_ff_1 (.clk(Clock), .D(nand_1_out), .Q(ToPeg_Byte_1), .en(row_d));  // open: Qn, preset, reset
  nand nand_1 (nand_1_out, ToPeg_Byte_1, FromPeg_Byte_1);
  D_Flip_Flop d_ff_2 (.clk(Clock), .D(nand_2_out), .Q(ToPeg_Byte_0), .en(row_d));  // open: Qn, preset, reset
  nand nand_2 (nand_2_out, ToPeg_Byte_0, FromPeg_Byte_0);
  D_Flip_Flop d_ff_3 (.clk(Clock), .D(ToPeg_Byte_1), .Q(FromPeg_Byte_1), .en(row_d));  // open: Qn, preset, reset
  D_Flip_Flop d_ff_4 (.clk(Clock), .D(ToPeg_Byte_0), .Q(FromPeg_Byte_0), .en(row_d));  // open: Qn, preset, reset
  and and_1 (out_3[0], row_d, ToPeg_Byte_0);
  and and_2 (out_3[1], row_d, ToPeg_Byte_1);
  and and_3 (out_3[2], row_d, FromPeg_Byte_0);
  and and_4 (out_3[3], row_d, FromPeg_Byte_1);

  // Notes on the sheet:
  //   ToPeg
  //   FromPeg
  //   Byte 1
  //   Byte 0
endmodule

module Final (
  input  in_1
);

  wire clock_1_out, main_1_out_3, main_1_out_4, main_1_top, n7_segment_1_out_4, n7_segment_1_out_5,
       n7_segment_1_out_6, n7_segment_1_out_7, n7_segment_1_out_8, n7_segment_2_out_4, n7_segment_2_out_5,
       n7_segment_2_out_6, n7_segment_2_out_7, n7_segment_2_out_8;
  wire [3:0] display_1_out_3, display_2_out_3, display_3_out_3, display_4_out_3, or_1_out;

  Clock clock_1 (.out(clock_1_out));
  main main_1 (.in_1(clock_1_out), .Top(main_1_top), .out_3(main_1_out_3), .out_4(main_1_out_4));  // open: Bottom
  Display display_1 (
    .row_d(in_1), .Clock(clock_1_out), .out_3(display_1_out_3));  // open: ToPeg_Byte_1, ToPeg_Byte_0, FromPeg_Byte_1, FromPeg_Byte_0
  Display display_2 (
    .row_d(main_1_out_4), .Clock(clock_1_out), .out_3(display_2_out_3));  // open: ToPeg_Byte_1, ToPeg_Byte_0, FromPeg_Byte_1, FromPeg_Byte_0
  Display display_3 (
    .row_d(main_1_out_3), .Clock(clock_1_out), .out_3(display_3_out_3));  // open: ToPeg_Byte_1, ToPeg_Byte_0, FromPeg_Byte_1, FromPeg_Byte_0
  Display display_4 (
    .row_d(main_1_top), .Clock(clock_1_out), .out_3(display_4_out_3));  // open: ToPeg_Byte_1, ToPeg_Byte_0, FromPeg_Byte_1, FromPeg_Byte_0
  _7_Segment_Display u_7_segment_display_1 (
    .g(n7_segment_1_out_8), .f(n7_segment_1_out_7), .a(n7_segment_1_out_5), .b(1'b1), .e(n7_segment_1_out_6),
    .d(n7_segment_1_out_5), .c(n7_segment_1_out_4));  // open: dp
  assign or_1_out = display_1_out_3 | display_2_out_3 | display_3_out_3 | display_4_out_3;  // OR_Gate or_1, 4 bits wide
  _7_segment u_7_segment_1 (
    .a(or_1_out[3]), .b(or_1_out[2]), .Clock(clock_1_out), .out_4(n7_segment_1_out_4),
    .out_5(n7_segment_1_out_5), .out_6(n7_segment_1_out_6), .out_7(n7_segment_1_out_7),
    .out_8(n7_segment_1_out_8));
  _7_segment u_7_segment_2 (
    .a(or_1_out[1]), .b(or_1_out[0]), .Clock(clock_1_out), .out_4(n7_segment_2_out_4),
    .out_5(n7_segment_2_out_5), .out_6(n7_segment_2_out_6), .out_7(n7_segment_2_out_7),
    .out_8(n7_segment_2_out_8));
  _7_Segment_Display u_7_segment_display_2 (
    .g(n7_segment_2_out_8), .f(n7_segment_2_out_7), .a(n7_segment_2_out_5), .b(1'b1), .e(n7_segment_2_out_6),
    .d(n7_segment_2_out_5), .c(n7_segment_2_out_4));  // open: dp

  // Notes on the sheet:
  //   Note :
  //   The T flip-flop corresponding to
  //   FromPeg Byte 0 should be initialised to 1
  //   FromPeg Byte 1 should be initialised to 0
  //   ToPeg Byte 0 should be initialised to 1
  //   ToPeg Byte 1 should be initialised to 1
  //   In 2, the T flip-flops should be initialised to
  //   FromPeg Byte 0 should be initialised to 1
  //   FromPeg Byte 1 should be initialised to 0
  //   ToPeg Byte 0 should be initialised to 0
  //   ToPeg Byte 1 should be initialised to 1
  //   Bottom
  //   4
  //   3
  //   2
  //   1
  //   The 4 instances of the subcircuit named display are labeled 1,2,3 and 4 respectively. In 1 and 3, the T flip-flops have to be initialised in such a manner as:
  //   After which, on changing the clock signals, the correct sequence of steps to solve the Tower of Hanoi problem for n = 3 disks is shown on the 7-segment display.
endmodule

module _7_segment (
  input  a,
  input  b,
  input  Clock,
  output out_4,
  output out_5,
  output out_6,
  output out_7,
  output out_8
);

  wire and_1_out, and_2_out, not_1_out, not_2_out, not_3_out, not_4_out, or_1_out, or_2_out;

  not not_1 (not_1_out, a);
  not not_2 (not_2_out, b);
  not not_3 (not_3_out, Clock);
  or or_1 (or_1_out, not_1_out, b);
  or or_2 (or_2_out, not_2_out, a);
  and and_1 (and_1_out, not_2_out, not_1_out);
  and and_2 (and_2_out, or_2_out, not_3_out, a, or_1_out);
  not not_4 (not_4_out, and_2_out);
  or or_3 (out_4, or_1_out, and_2_out);
  and and_3 (out_5, or_2_out, not_4_out);
  and and_4 (out_6, not_2_out, not_4_out);
  or or_4 (out_7, and_1_out, and_2_out);
  or or_5 (out_8, a, and_2_out);

  // Notes on the sheet:
  //   c
  //   a,d
  //   e
  //   f
  //   g
endmodule
